// Logisim project sCPU.circ as structural Verilog: 2 circuits, main circuit main
module main (
  input  [1:0] in_1,
  input  in_2,
  input  in_3,
  output [7:0] out_4
);

  wire clock_1_out;

  Clock clock_1 (.out(clock_1_out));
  ROM4x8 rom4x8_1 (.address(in_1), .WE(in_2), .CLK(clock_1_out), .R(in_3), .out_5(out_4));
endmodule

module ROM4x8 (
  input  [1:0] address,
  input  WE,
  input  CLK,
  input  R,
  output [7:0] out_5
);

  wire [7:0] r1_q, r2_q, r3_q, r4_q;

  Register r1 (.D(8'h8a), .en(WE), .clk(CLK), .Q(r1_q), .clr(R));
  Register r2 (.D({8{1'b1}}), .en(WE), .clk(CLK), .Q(r2_q), .clr(R));
  Register r4 (.D({8{1'b0}}), .en(WE), .clk(CLK), .Q(r4_q), .clr(R));
  Register r3 (.D({8{1'b0}}), .en(WE), .clk(CLK), .Q(r3_q), .clr(R));
  Multiplexer #(.select(2), .width(8)) multiplexer_1 (
    .in0(r1_q), .in1(r2_q), .in2(r4_q), .in3(r3_q), .out(out_5), .sel(address));

  // Notes on the sheet:
  //   li r0 10
  //   随便输入的
endmodule
